# Fritzing sketch ArduinoUnoPatch (saved by Fritzing 0.7.12b)
breadboards: 1

parts:
  Arduino1 = Arduino
  Componente1 = SRF05 Ultrasonic Rangefinder
  Componente2 = SRF05 Ultrasonic Rangefinder

nets:
  N1: Arduino1.D6, Componente1.Trigger_Input
  N2: Arduino1.D5, Componente1.Echo_Output
  N3: Arduino1.D3, Componente2.Trigger_Input
  N4: Arduino1.D2, Componente2.Echo_Output
  N5: Arduino1.+5V, Componente1.5v_Supply, Componente2.5v_Supply
  N6: Arduino1.GND, Componente1.Ground, Componente2.Ground
